# Fritzing sketch PIR (saved by Fritzing 0.9.3b)
breadboards: 1

parts:
  Part1 = Arduino Mega 2560 (Rev3)
  R1 = Resistor [tolerance=±5% resistance=220 package="0603 [SMD]"]
  R2 = Resistor [tolerance=±5% resistance=220 package="0603 [SMD]"]
  LED1 = smd LED [color="Red (633nm)" package="1206 [SMD]"]
  LED2 = smd LED [color="Red (633nm)" package="1206 [SMD]"]
  R3 = Resistor [tolerance=±5% resistance=220 package="0603 [SMD]"]  # not connected
  PIR1 = PIR sensor  # not connected

nets:
  N1: Part1.D13_PWM, LED1.anode, LED2.anode
  N2: Part1.GND, R1.Pin_1, R2.Pin_1
  N3: R1.Pin_0, LED2.cathode
  N4: R2.Pin_0, LED1.cathode
